// Logisim project Mikaelle_Costa_de_Sanatana (16 bits).circ as structural Verilog: 20 circuits, main circuit main
module main (
  input  in_1
);

  wire and_1_out, comparator_1_eq, data, flag_1_out_6, flag_1_out_7, flag_1_out_8, flag_1_out_9, in_out,
       io_e, io_s, monitor_1_out_6, monitor_1_out_7, or_1_out, register_1_q, teclado_1_out_8,
       teclado_1_out_9, uc_1_out_6, uc_1_out_7, uc_1_out_8, uc_1_out_9, uc_1_out_10, uc_1_out_11,
       uc_1_out_12, uc_1_out_13, uc_1_out_14, uc_1_out_15, uc_1_out_17, uc_1_out_18, uc_1_out_19,
       uc_1_out_20, uc_1_out_21, uc_1_out_22, uc_1_out_23, uc_1_out_24, uc_1_out_25, uc_1_out_26,
       ula_1_aequalb, ula_1_amaiorb, ula_1_carryout, ula_1_zero;
  wire [2:0] uc_1_out_16;
  wire [6:0] keyboard_1_data, monitor_1_out_5;
  wire [15:0] ACC_q, b1_out_3, controlled_buffer_1_out, controlled_buffer_7_out, iar_q, ir_q, MAR_q, R0_q,
       R1_q, R2_q, R3_q, TMP_q, ula_1_out_5;

  ula ula_1 (
    .in_2(controlled_buffer_1_out), .in_3(b1_out_3), .out_5(ula_1_out_5), .in_1(uc_1_out_16),
    .carryout(ula_1_carryout), .zero(ula_1_zero), .amaiorb(ula_1_amaiorb), .aequalb(ula_1_aequalb));
  Register #(.width(16)) TMP (.D(controlled_buffer_1_out), .Q(TMP_q), .clk(uc_1_out_6));  // open: en, clr
  bus_1 b1 (.in_1(TMP_q), .out_3(b1_out_3), .in_2(uc_1_out_7));
  flag flag_1 (
    .in_1(ula_1_carryout), .in_2(ula_1_zero), .in_3(ula_1_amaiorb), .in_5(ula_1_aequalb),
    .out_6(flag_1_out_6), .out_7(flag_1_out_7), .out_8(flag_1_out_8), .out_9(flag_1_out_9), .in_4(uc_1_out_21));
  Register #(.width(16)) ACC (.D(ula_1_out_5), .Q(ACC_q), .clk(uc_1_out_22));  // open: en, clr
  assign controlled_buffer_1_out = uc_1_out_23 ? ACC_q : 16'bz;  // Controlled_Buffer controlled_buffer_1
  Keyboard keyboard_1 (.clk(teclado_1_out_8), .re(teclado_1_out_9), .data(keyboard_1_data));  // open: clr, avail
  teclado teclado_1 (
    .in_2(io_e), .in_4(io_s), .in_5(data), .in_6(in_out), .in_1(controlled_buffer_1_out),
    .out_7(controlled_buffer_1_out), .in_3(keyboard_1_data), .out_8(teclado_1_out_8), .out_9(teclado_1_out_9));
  Register #(.width(16)) R0 (.D(controlled_buffer_1_out), .Q(R0_q), .clk(uc_1_out_8));  // open: en, clr
  assign controlled_buffer_1_out = uc_1_out_9 ? R0_q : 16'bz;  // Controlled_Buffer controlled_buffer_2
  Register #(.width(16)) R1 (.D(controlled_buffer_1_out), .Q(R1_q), .clk(uc_1_out_10));  // open: en, clr
  uc uc_1 (
    .out_16(uc_1_out_16), .in_1(flag_1_out_6), .in_2(flag_1_out_7), .in_3(flag_1_out_8), .in_4(flag_1_out_9),
    .out_21(uc_1_out_21), .out_22(uc_1_out_22), .out_23(uc_1_out_23), .out_6(uc_1_out_6), .out_7(uc_1_out_7),
    .out_8(uc_1_out_8), .out_9(uc_1_out_9), .out_10(uc_1_out_10), .out_11(uc_1_out_11), .out_12(uc_1_out_12),
    .out_13(uc_1_out_13), .out_14(uc_1_out_14), .out_15(uc_1_out_15), .out_24(uc_1_out_24),
    .out_25(uc_1_out_25), .out_26(uc_1_out_26), .in_5(ir_q), .out_27(io_s), .out_28(io_e), .out_29(data),
    .out_30(in_out), .out_17(uc_1_out_17), .out_18(uc_1_out_18), .out_19(uc_1_out_19), .out_20(uc_1_out_20));
  LED led_1 (.in(uc_1_out_20));
  assign controlled_buffer_1_out = uc_1_out_11 ? R1_q : 16'bz;  // Controlled_Buffer controlled_buffer_3
  Register #(.width(16)) iar (.D(controlled_buffer_1_out), .Q(iar_q), .clk(uc_1_out_24));  // open: en, clr
  assign controlled_buffer_1_out = uc_1_out_25 ? iar_q : 16'bz;  // Controlled_Buffer controlled_buffer_4
  monitor monitor_1 (
    .in_2(io_s), .in_3(data), .in_4(in_out), .in_1(controlled_buffer_1_out), .out_5(monitor_1_out_5),
    .out_6(monitor_1_out_6), .out_7(monitor_1_out_7));
  Register #(.width(16)) ir (.D(controlled_buffer_1_out), .Q(ir_q), .clk(uc_1_out_26));  // open: en, clr
  TTY tty_1 (.data(monitor_1_out_5), .clk(monitor_1_out_6), .we(monitor_1_out_7), .clr(in_1));
  assign controlled_buffer_1_out = uc_1_out_13 ? R2_q : 16'bz;  // Controlled_Buffer controlled_buffer_5
  Register #(.width(16)) R2 (.D(controlled_buffer_1_out), .Q(R2_q), .clk(uc_1_out_12));  // open: en, clr
  assign controlled_buffer_1_out = uc_1_out_15 ? R3_q : 16'bz;  // Controlled_Buffer controlled_buffer_6
  Register #(.width(16)) R3 (.D(controlled_buffer_1_out), .Q(R3_q), .clk(uc_1_out_14));  // open: en, clr
  Register #(.width(16)) MAR (.D(controlled_buffer_1_out), .Q(MAR_q), .clk(uc_1_out_17));  // open: en, clr
  or or_1 (or_1_out, uc_1_out_18, uc_1_out_19);
  and and_1 (and_1_out, io_s, data, in_out);
  RAM #(.addrWidth(16), .dataWidth(16), .databus("bidir")) ram_1 (
    .addr(MAR_q), .we(uc_1_out_18), .oe(uc_1_out_19), .clk(or_1_out));  // open: data
  Comparator #(.width(16)) comparator_1 (.a(controlled_buffer_1_out), .b(16'h2), .eq(comparator_1_eq));  // open: gt, lt
  Register #(.width(1)) register_1 (.D(comparator_1_eq), .Q(register_1_q), .clk(and_1_out));  // open: en, clr
  assign controlled_buffer_7_out = io_s ? controlled_buffer_1_out : 16'bz;  // Controlled_Buffer controlled_buffer_7
  // PortIO #(.number(16)) portio_1: pin names not known; wires that end beside it: register_1_q, controlled_buffer_7_out

  // Notes on the sheet:
  //   Mikaelle Costa de Santana - 22401909
endmodule

module somador1bit (
  input  in_1,
  input  a,
  input  b,
  output out_4,
  output out_5
);

  wire and_1_out, and_2_out, and_3_out, xor_1_out;

  xor xor_1 (xor_1_out, a, b);
  and and_1 (and_1_out, a, in_1);
  and and_2 (and_2_out, a, b);
  and and_3 (and_3_out, b, in_1);
  xor xor_2 (out_4, xor_1_out, in_1);
  or or_1 (out_5, and_1_out, and_2_out, and_3_out);
endmodule

module somador8bit (
  input  in_1,
  input  [7:0] in_2,
  input  [7:0] in_3,
  output [7:0] out_4,
  output out_5
);

  wire somador1bit_1_out_5, somador1bit_2_out_5, somador1bit_3_out_5, somador1bit_4_out_5,
       somador1bit_5_out_5, somador1bit_6_out_5, somador1bit_7_out_5;

  somador1bit somador1bit_1 (.a(in_2[0]), .b(in_3[0]), .in_1(in_1), .out_4(out_4[0]), .out_5(somador1bit_1_out_5));
  somador1bit somador1bit_2 (
    .a(in_2[1]), .b(in_3[1]), .in_1(somador1bit_1_out_5), .out_4(out_4[1]), .out_5(somador1bit_2_out_5));
  somador1bit somador1bit_3 (
    .a(in_2[2]), .b(in_3[2]), .in_1(somador1bit_2_out_5), .out_4(out_4[2]), .out_5(somador1bit_3_out_5));
  somador1bit somador1bit_4 (
    .a(in_2[3]), .b(in_3[3]), .in_1(somador1bit_3_out_5), .out_4(out_4[3]), .out_5(somador1bit_4_out_5));
  somador1bit somador1bit_5 (
    .a(in_2[4]), .b(in_3[4]), .in_1(somador1bit_4_out_5), .out_4(out_4[4]), .out_5(somador1bit_5_out_5));
  somador1bit somador1bit_6 (
    .a(in_2[5]), .b(in_3[5]), .in_1(somador1bit_5_out_5), .out_4(out_4[5]), .out_5(somador1bit_6_out_5));
  somador1bit somador1bit_7 (
    .a(in_2[6]), .b(in_3[6]), .in_1(somador1bit_6_out_5), .out_4(out_4[6]), .out_5(somador1bit_7_out_5));
  somador1bit somador1bit_8 (.a(in_2[7]), .b(in_3[7]), .in_1(somador1bit_7_out_5), .out_4(out_4[7]), .out_5(out_5));
endmodule

module memory1bit (
  input  in_1,
  input  in_2,
  output out_3
);

  wire nand_1_out, nand_2_out, nand_3_out;

  nand nand_1 (nand_1_out, in_1, in_2);
  nand nand_2 (nand_2_out, nand_1_out, in_2);
  nand nand_3 (nand_3_out, out_3, nand_2_out);
  nand nand_4 (out_3, nand_1_out, nand_3_out);
endmodule

module memory8bit (
  input  [7:0] in_1,
  input  in_2,
  output [7:0] out_3
);

  memory1bit memory1bit_1 (.in_1(in_1[0]), .in_2(in_2), .out_3(out_3[0]));
  memory1bit memory1bit_2 (.in_1(in_1[1]), .in_2(in_2), .out_3(out_3[1]));
  memory1bit memory1bit_3 (.in_1(in_1[2]), .in_2(in_2), .out_3(out_3[2]));
  memory1bit memory1bit_4 (.in_1(in_1[3]), .in_2(in_2), .out_3(out_3[3]));
  memory1bit memory1bit_5 (.in_1(in_1[4]), .in_2(in_2), .out_3(out_3[4]));
  memory1bit memory1bit_6 (.in_1(in_1[5]), .in_2(in_2), .out_3(out_3[5]));
  memory1bit memory1bit_7 (.in_1(in_1[6]), .in_2(in_2), .out_3(out_3[6]));
  memory1bit memory1bit_8 (.in_1(in_1[7]), .in_2(in_2), .out_3(out_3[7]));
endmodule

module enable (
  input  [7:0] in_1,
  input  in_2,
  output [7:0] out_3
);

  assign out_3 = in_2 ? in_1 : 8'bz;  // Controlled_Buffer controlled_buffer_1
endmodule

module registrador_set_enable (
  input  [7:0] in_1,
  input  in_2,
  input  in_3,
  output [7:0] out_4
);

  wire [7:0] memory8bit_1_out_3;

  memory8bit memory8bit_1 (.in_1(in_1), .in_2(in_2), .out_3(memory8bit_1_out_3));
  enable enable_1 (.in_1(memory8bit_1_out_3), .in_2(in_3), .out_3(out_4));
endmodule

module decode2x4 (
  input  in_1,
  input  in_2,
  output out_3,
  output out_4,
  output out_5,
  output out_6
);

  wire not_1_out, not_2_out;

  not not_1 (not_1_out, in_1);
  not not_2 (not_2_out, in_2);
  and and_1 (out_3, not_1_out, not_2_out);
  and and_2 (out_4, in_1, not_2_out);
  and and_3 (out_5, in_2, not_1_out);
  and and_4 (out_6, in_1, in_2);
endmodule

module decode4x16 (
  input  [7:0] in_1,
  input  we,
  input  oe,
  input  [7:0] in_4
);

  wire and_1_out, and_2_out, and_3_out, decoder_1_out0, decoder_2_out0;
  wire [7:0] registrador_set_enable_1_out_4;

  Decoder #(.enable("false"), .select(4)) decoder_1 (
    .out0(decoder_1_out0), .sel(in_1[7:4]));  // open: out1, out2, out3, out4, out5, out6, out7, out8, out9, out10, out11, out12, out13, out14, out15
  Decoder #(.enable("false"), .select(4)) decoder_2 (
    .out0(decoder_2_out0), .sel(in_1[3:0]));  // open: out1, out2, out3, out4, out5, out6, out7, out8, out9, out10, out11, out12, out13, out14, out15
  and and_1 (and_1_out, decoder_2_out0, decoder_1_out0);
  and and_2 (and_2_out, and_1_out, we);
  and and_3 (and_3_out, and_1_out, oe);
  registrador_set_enable registrador_set_enable_1 (
    .in_1(in_4), .in_2(and_2_out), .in_3(and_3_out), .out_4(registrador_set_enable_1_out_4));
endmodule

module memory256 (
  input  in_1,
  input  [7:0] in_2,
  input  in_3,
  input  in_4,
  input  in_5,
  input  in_6,
  input  in_7,
  input  in_8
);

  wire or_1_out;
  wire [7:0] register_1_q, registrador_set_enable_1_out_4;

  // Probe on registrador_set_enable_1_out_4
  registrador_set_enable registrador_set_enable_1 (
    .in_1(in_2), .in_2(in_3), .in_3(in_5), .out_4(registrador_set_enable_1_out_4));
  registrador_set_enable registrador_set_enable_2 (
    .in_1(registrador_set_enable_1_out_4), .in_2(in_4), .in_3(in_6), .out_4(registrador_set_enable_1_out_4));
  or or_1 (or_1_out, in_7, in_8);
  Register register_1 (.D(registrador_set_enable_1_out_4), .Q(register_1_q), .clk(in_1));  // open: en, clr
  RAM ram_1 (
    .addr(register_1_q), .we(in_7), .oe(in_8), .clk(or_1_out), .din(registrador_set_enable_1_out_4),
    .dout(registrador_set_enable_1_out_4));
endmodule

module shiftright (
  input  [15:0] in_1,
  input  in_2,
  output out_3,
  output [15:0] out_4
);


  assign out_3 = in_1[0];
  assign out_4 = {in_2, in_1[15:1]};
endmodule

module shiftleft (
  input  in_1,
  input  [15:0] in_2,
  output [15:0] out_3,
  output out_4
);


  assign out_3 = {in_2[14:0], in_1};
  assign out_4 = in_2[15];
endmodule

module ula (
  input  [2:0] in_1,
  input  [15:0] in_2,
  input  [15:0] in_3,
  output carryout,
  output [15:0] out_5,
  output zero,
  output amaiorb,
  output aequalb
);

  wire adder_1_cout, shiftleft_1_out_4, shiftright_1_out_3;
  wire [15:0] adder_1_out, and_1_out, not_1_out, or_1_out, shiftleft_1_out_3, shiftright_1_out_4, xor_1_out;

  shiftright shiftright_1 (.in_1(in_2), .out_3(shiftright_1_out_3), .in_2(1'b0), .out_4(shiftright_1_out_4));
  shiftleft shiftleft_1 (.in_2(in_2), .in_1(1'b0), .out_4(shiftleft_1_out_4), .out_3(shiftleft_1_out_3));
  Adder #(.width(16)) adder_1 (.a(in_2), .b(in_3), .out(adder_1_out), .cin(1'b0), .cout(adder_1_cout));
  assign not_1_out = ~in_2;  // NOT_Gate not_1, 16 bits wide
  assign and_1_out = in_2 & in_3;  // AND_Gate and_1, 16 bits wide
  assign or_1_out = in_2 | in_3;  // OR_Gate or_1, 16 bits wide
  assign xor_1_out = in_2 ^ in_3;  // XOR_Gate xor_1, 16 bits wide
  Comparator #(.width(16)) comparator_1 (.a(in_2), .b(in_3), .gt(amaiorb), .eq(aequalb));  // open: lt
  Multiplexer #(.select(3)) multiplexer_1 (
    .in0(adder_1_cout), .in1(shiftright_1_out_3), .in2(shiftleft_1_out_4), .in3(1'b0), .in4(1'b0),
    .in5(1'b0), .in6(1'b0), .in7(1'b0), .out(carryout), .sel(in_1));
  Multiplexer #(.select(3), .width(16)) multiplexer_2 (
    .in0(adder_1_out), .in1(shiftright_1_out_4), .in2(shiftleft_1_out_3), .in3(not_1_out), .in4(and_1_out),
    .in5(or_1_out), .in6(xor_1_out), .in7(in_2), .out(out_5), .sel(in_1));
  nor nor_1 (zero, out_5[0], out_5[1], out_5[2], out_5[3], out_5[4], out_5[5], out_5[6], out_5[7], out_5[8], out_5[9], out_5[10], out_5[11], out_5[12], out_5[13], out_5[14], out_5[15]);
endmodule

module bus_1 (
  input  [15:0] in_1,
  input  in_2,
  output [15:0] out_3
);

  Multiplexer #(.width(16)) multiplexer_1 (.in0(in_1), .in1(16'h1), .out(out_3), .sel(in_2));
endmodule

module clk (
  output set,
  output enable
);

  wire c1_out, not_1_out, t_ff_1_q;

  Clock c1 (.out(c1_out));
  not not_1 (not_1_out, c1_out);
  T_Flip_Flop t_ff_1 (.clk(c1_out), .T(1'b1), .Q(t_ff_1_q));  // open: Qn, preset, reset
  and and_1 (set, not_1_out, t_ff_1_q);
  or or_1 (enable, t_ff_1_q, c1_out);
endmodule

module stepper (
  input  in_1,
  output s2,
  output s1,
  output s3,
  output s4,
  output s5,
  output s6,
  output init
);

  wire decoder_1_out7;
  wire [2:0] counter_1_q;

  Counter #(.max('h7), .width(3)) counter_1 (
    .D(3'b000), .Q(counter_1_q), .clk(in_1), .clr(decoder_1_out7));  // open: load, count, carry, up
  Decoder #(.enable("false"), .select(3)) decoder_1 (
    .out0(init), .out1(s1), .out2(s2), .out3(s3), .out4(s4), .out5(s5), .out6(s6), .out7(decoder_1_out7),
    .sel(counter_1_q));
endmodule

module flag (
  input  in_1,
  input  in_2,
  input  in_3,
  input  in_4,
  input  in_5,
  output out_6,
  output out_7,
  output out_8,
  output out_9
);

  Register #(.width(4)) register_1 (
    .D({in_5, in_3, in_2, in_1}), .Q({out_9, out_8, out_7, out_6}), .clk(in_4));  // open: en, clr
endmodule

module uc (
  input  in_1,
  input  in_2,
  input  in_3,
  input  in_4,
  input  [15:0] in_5,
  output out_6,
  output out_7,
  output out_8,
  output out_9,
  output out_10,
  output out_11,
  output out_12,
  output out_13,
  output out_14,
  output out_15,
  output [2:0] out_16,
  output out_17,
  output out_18,
  output out_19,
  output out_20,
  output out_21,
  output out_22,
  output out_23,
  output out_24,
  output out_25,
  output out_26,
  output out_27,
  output out_28,
  output out_29,
  output out_30
);

  wire A_out, and_5_out, and_6_out, and_7_out, and_8_out, and_9_out, and_10_out, and_11_out, and_12_out,
       and_16_out, and_17_out, and_18_out, and_19_out, and_20_out, and_21_out, and_22_out, and_23_out,
       and_24_out, and_25_out, and_26_out, and_27_out, and_28_out, and_29_out, and_30_out, and_31_out,
       and_32_out, and_33_out, and_34_out, and_35_out, and_36_out, and_37_out, and_38_out, and_39_out,
       and_40_out, and_41_out, and_42_out, and_43_out, C_out, clk_1_enable, clk_1_set, decoder_1_out0,
       decoder_1_out1, decoder_1_out2, decoder_1_out3, decoder_2_out0, decoder_2_out1, decoder_2_out2,
       decoder_2_out3, decoder_3_out0, decoder_3_out1, decoder_3_out2, decoder_3_out3, decoder_3_out4,
       decoder_3_out5, decoder_3_out6, decoder_3_out7, decoder_4_out0, decoder_4_out1, decoder_4_out2,
       decoder_4_out3, E_out, not_1_out, not_2_out, not_3_out, or_6_out, or_7_out, or_8_out, or_9_out,
       or_10_out, or_11_out, or_12_out, or_13_out, ra_e_out, rb_e_out, rb_s_out, stepper_1_s1, stepper_1_s2,
       stepper_1_s3, stepper_1_s4, stepper_1_s5, stepper_1_s6, Z_out;

  clk clk_1 (.set(clk_1_set), .enable(clk_1_enable));
  and and_1 (out_25, clk_1_enable, or_6_out);
  and and_2 (out_19, clk_1_enable, or_7_out);
  and and_3 (out_23, clk_1_enable, or_8_out);
  and and_4 (out_28, clk_1_enable, and_40_out);
  or or_1 (out_9, and_5_out, and_9_out);
  or or_2 (out_11, and_6_out, and_10_out);
  or or_3 (out_13, and_7_out, and_11_out);
  or or_4 (out_15, and_8_out, and_12_out);
  and and_5 (and_5_out, clk_1_enable, rb_e_out, decoder_1_out0);
  and and_6 (and_6_out, clk_1_enable, rb_e_out, decoder_1_out1);
  and and_7 (and_7_out, clk_1_enable, rb_e_out, decoder_1_out2);
  and and_8 (and_8_out, clk_1_enable, rb_e_out, decoder_1_out3);
  and and_9 (and_9_out, clk_1_enable, ra_e_out, decoder_2_out0);
  and and_10 (and_10_out, clk_1_enable, ra_e_out, decoder_2_out1);
  and and_11 (and_11_out, clk_1_enable, ra_e_out, decoder_2_out2);
  and and_12 (and_12_out, clk_1_enable, ra_e_out, decoder_2_out3);
  or or_5 (out_7, stepper_1_s1, and_32_out, and_31_out, and_28_out);
  or or_6 (or_6_out, stepper_1_s1, and_28_out, and_30_out, and_31_out);
  or or_7 (or_7_out, stepper_1_s2, and_43_out, and_38_out, and_37_out, and_35_out);
  or or_8 (or_8_out, stepper_1_s3, and_39_out, and_42_out, and_41_out);
  or rb_e (rb_e_out, and_25_out, and_36_out, and_29_out, and_33_out);
  or ra_e (ra_e_out, and_27_out, and_26_out, and_34_out);
  and and_13 (out_16[0], stepper_1_s5, in_5[15], in_5[12]);
  and and_14 (out_16[1], stepper_1_s5, in_5[15], in_5[13]);
  and and_15 (out_16[2], stepper_1_s5, in_5[15], in_5[14]);
  Decoder #(.enable("false"), .select(2)) decoder_1 (
    .out0(decoder_1_out0), .out1(decoder_1_out1), .out2(decoder_1_out2), .out3(decoder_1_out3),
    .sel(in_5[1:0]));
  Decoder #(.enable("false"), .select(2)) decoder_2 (
    .out0(decoder_2_out0), .out1(decoder_2_out1), .out2(decoder_2_out2), .out3(decoder_2_out3),
    .sel(in_5[3:2]));
  not not_1 (not_1_out, in_5[15]);
  Decoder #(.enable("false"), .select(3)) decoder_3 (
    .out0(decoder_3_out0), .out1(decoder_3_out1), .out2(decoder_3_out2), .out3(decoder_3_out3),
    .out4(decoder_3_out4), .out5(decoder_3_out5), .out6(decoder_3_out6), .out7(decoder_3_out7),
    .sel(in_5[14:12]));
  and and_16 (and_16_out, not_1_out, decoder_3_out0);
  and and_17 (and_17_out, not_1_out, decoder_3_out1);
  and and_18 (and_18_out, not_1_out, decoder_3_out2);
  and and_19 (and_19_out, not_1_out, decoder_3_out3);
  and and_20 (and_20_out, not_1_out, decoder_3_out4);
  and and_21 (and_21_out, not_1_out, decoder_3_out5);
  and and_22 (and_22_out, not_1_out, decoder_3_out6);
  and and_23 (and_23_out, not_1_out, decoder_3_out7);
  and C (C_out, in_5[3], in_1);
  and A (A_out, in_5[2], in_2);
  and E (E_out, in_5[1], in_3);
  and Z (Z_out, in_5[0], in_4);
  and and_24 (and_24_out, in_5[12], in_5[13], in_5[14]);
  not not_2 (not_2_out, and_24_out);
  stepper stepper_1 (
    .in_1(clk_1_enable), .s1(stepper_1_s1), .s2(stepper_1_s2), .s3(stepper_1_s3), .s4(stepper_1_s4),
    .s5(stepper_1_s5), .s6(stepper_1_s6), .init(out_20));
  and and_25 (and_25_out, stepper_1_s4, in_5[15]);
  and and_26 (and_26_out, stepper_1_s4, and_16_out);
  and and_27 (and_27_out, stepper_1_s4, and_17_out);
  and and_28 (and_28_out, stepper_1_s4, and_18_out);
  and and_29 (and_29_out, stepper_1_s4, and_19_out);
  and and_30 (and_30_out, stepper_1_s4, and_20_out);
  and and_31 (and_31_out, stepper_1_s4, and_21_out);
  and and_32 (and_32_out, stepper_1_s4, and_22_out);
  and and_33 (and_33_out, stepper_1_s4, and_23_out, in_5[3]);
  not not_3 (not_3_out, in_5[3]);
  or or_9 (or_9_out, C_out, A_out, E_out, Z_out);
  and and_34 (and_34_out, stepper_1_s5, in_5[15]);
  and and_35 (and_35_out, stepper_1_s5, and_16_out);
  and and_36 (and_36_out, stepper_1_s5, and_17_out);
  and and_37 (and_37_out, stepper_1_s5, and_18_out);
  and and_38 (and_38_out, stepper_1_s5, and_20_out);
  and and_39 (and_39_out, stepper_1_s5, and_21_out);
  and and_40 (and_40_out, stepper_1_s5, and_23_out, not_3_out);
  and and_41 (and_41_out, stepper_1_s6, in_5[15], not_2_out);
  and and_42 (and_42_out, stepper_1_s6, and_18_out);
  and and_43 (and_43_out, stepper_1_s6, and_21_out, or_9_out);
  Decoder #(.enable("false"), .select(2)) decoder_4 (
    .out0(decoder_4_out0), .out1(decoder_4_out1), .out2(decoder_4_out2), .out3(decoder_4_out3),
    .sel(in_5[1:0]));
  or or_10 (or_10_out, stepper_1_s1, and_28_out, and_31_out, and_26_out, and_27_out, and_30_out);
  or or_11 (or_11_out, stepper_1_s3, and_29_out, and_38_out, and_39_out, and_42_out, and_43_out);
  or or_12 (or_12_out, stepper_1_s1, and_28_out, and_31_out, and_34_out);
  or or_13 (or_13_out, and_32_out, and_34_out);
  or rb_s (rb_s_out, and_35_out, and_41_out, and_37_out, and_40_out);
  and and_44 (out_26, clk_1_set, stepper_1_s2);
  and and_45 (out_17, clk_1_set, or_10_out);
  and and_46 (out_24, clk_1_set, or_11_out);
  and and_47 (out_22, clk_1_set, or_12_out);
  and and_48 (out_18, clk_1_set, and_36_out);
  and and_49 (out_6, clk_1_set, and_25_out);
  and and_50 (out_21, clk_1_set, or_13_out);
  and and_51 (out_27, clk_1_set, and_33_out);
  and and_52 (out_8, clk_1_set, rb_s_out, decoder_4_out0);
  and and_53 (out_10, clk_1_set, rb_s_out, decoder_4_out1);
  and and_54 (out_12, clk_1_set, rb_s_out, decoder_4_out2);
  and and_55 (out_14, clk_1_set, rb_s_out, decoder_4_out3);

  assign out_29 = in_5[2];
  assign out_30 = in_5[3];

  // Other names for the same wires on the sheet: ir[15:0] = in_5; acc_e = out_23; acc_s = out_22; bus_1 = out_7;
  //   carry_out = in_1; equal = in_3; flags_s = out_21; iar_e = out_25; iar_s = out_24; init = out_20;
  //   IO_clk_e = out_28; IO_clk_s = out_27; data = in_5[2]; in_out = in_5[3]; ir_s = out_26; larger = in_2;
  //   mar_s = out_17; R0_e = out_9; R0_s = out_8; R1_e = out_11; R1_s = out_10; R2_e = out_13; R2_s = out_12;
  //   R3_e = out_15; R3_s = out_14; ram_e = out_19; ram_s = out_18; tmp_s = out_6; ula[2:0] = out_16; zero = in_4
endmodule

module teclado (
  input  [15:0] in_1,
  input  in_2,
  input  [6:0] in_3,
  input  in_4,
  input  in_5,
  input  in_6,
  output [15:0] out_7,
  output out_8,
  output out_9
);

  wire and_1_out, comparator_1_eq;
  wire [15:0] bit_extender_1_out;

  Comparator #(.width(16)) comparator_1 (.a(in_1), .b({16{1'b0}}), .eq(comparator_1_eq));  // open: gt, lt
  and and_1 (and_1_out, in_4, in_5, in_6);
  Register #(.width(1)) register_1 (.D(comparator_1_eq), .Q(out_9), .clk(and_1_out));  // open: en, clr
  T_Flip_Flop t_ff_1 (.clk(in_2), .T(1'b1), .Qn(out_8));  // open: Q, preset, reset
  // Probe on out_7
  assign out_7 = in_2 ? bit_extender_1_out : 16'bz;  // Controlled_Buffer controlled_buffer_1
  assign bit_extender_1_out = {{9{1'b0}}, in_3};  // Bit_Extender bit_extender_1
  // Probe on in_3
endmodule

module monitor (
  input  [15:0] in_1,
  input  in_2,
  input  in_3,
  input  in_4,
  output [6:0] out_5,
  output out_6,
  output out_7
);

  wire and_1_out, comparator_1_eq;

  Comparator #(.width(16)) comparator_1 (.a(in_1), .b(16'h1), .eq(comparator_1_eq));  // open: gt, lt
  and and_1 (and_1_out, in_2, in_3, in_4);
  Bit_Extender #(.in_width(16), .out_width(7), .\type ("zero")) bit_extender_1 (.in(in_1), .out(out_5));
  Register #(.width(1)) register_1 (.D(comparator_1_eq), .Q(out_7), .clk(and_1_out));  // open: en, clr

  assign out_6 = in_2;
endmodule
